# Fritzing sketch platineEssaiEsp8266 (saved by Fritzing 0.9.3b)
breadboards: 1

parts:
  S3 = Pushbutton [package="[SMD]"]
  U2 = Nodemcu Breakout [part_number=nodemcu]

nets:
  N1: S3.Pin_1, S3.Pin_2
  N2: S3.Pin_3, S3.Pin_4
  3V3: U2.3V3, U2.3.3V

custom parts:
  Nodemcu Breakout: Nodemcu Breakout Board Based on ESP8266 ESP-12E module with onboard PCB antenna and USB/UART connector
